// Logisim project AndOrNotNAND.circ as structural Verilog: 1 circuit, main circuit main
module main (
  input  X,
  input  Y,
  output out_3,
  output out_4,
  output out_5,
  output out_6,
  output out_7,
  output out_8
);

  wire nand_1_out, nand_2_out, nand_3_out;

  nand nand_1 (nand_1_out, X, Y);
  nand nand_2 (nand_2_out, X, X);
  nand nand_3 (nand_3_out, Y, Y);
  nand nand_4 (out_3, X, X);
  not not_1 (out_4, X);
  and and_1 (out_5, X, Y);
  or or_1 (out_7, X, Y);
  nand nand_5 (out_6, nand_1_out, nand_1_out);
  nand nand_6 (out_8, nand_2_out, nand_3_out);
endmodule
