// Logisim project adder4A.circ as structural Verilog: 1 circuit, main circuit main
module main (
  input  X_3,
  input  X_2,
  input  X_1,
  input  X_0,
  input  Y_3,
  input  Y_2,
  input  Y_1,
  input  Y_0,
  output C,
  output S_3,
  output S_2,
  output S_1,
  output S_0
);

  wire and_1_out, and_2_out, and_3_out, and_4_out, and_5_out, and_6_out, and_7_out, or_2_out, or_3_out,
       xor_1_out, xor_3_out, xor_5_out;

  and and_1 (and_1_out, Y_3, X_3);
  or or_1 (C, and_1_out, and_2_out);
  xor xor_1 (xor_1_out, Y_3, X_3);
  and and_2 (and_2_out, xor_1_out, or_2_out);
  and and_3 (and_3_out, Y_2, X_2);
  or or_2 (or_2_out, and_3_out, and_5_out);
  xor xor_2 (S_3, xor_1_out, or_2_out);
  xor xor_3 (xor_3_out, Y_2, X_2);
  and and_4 (and_4_out, Y_1, X_1);
  and and_5 (and_5_out, or_3_out, xor_3_out);
  or or_3 (or_3_out, and_4_out, and_6_out);
  xor xor_4 (S_2, xor_3_out, or_3_out);
  xor xor_5 (xor_5_out, Y_1, X_1);
  and and_6 (and_6_out, xor_5_out, and_7_out);
  xor xor_6 (S_1, xor_5_out, and_7_out);
  and and_7 (and_7_out, Y_0, X_0);
  xor xor_7 (S_0, Y_0, X_0);
endmodule
