// Logisim project decoder2bit.circ as structural Verilog: 1 circuit, main circuit main
module main (
  input  [1:0] Address,
  input  in_2,
  input  MSB,
  input  LSB,
  output Line_0,
  output Line_1,
  output Line_2,
  output Line_3,
  output Line_3_2,
  output Line_2_2,
  output Line_1_2,
  output Line_0_2
);

  wire not_1_out, not_2_out;

  Decoder #(.select(2)) decoder_1 (
    .out0(Line_0), .out1(Line_1), .out2(Line_2), .out3(Line_3), .sel(Address), .en(in_2));
  not not_1 (not_1_out, MSB);
  not not_2 (not_2_out, LSB);
  and and_1 (Line_3_2, MSB, LSB);
  and and_2 (Line_2_2, MSB, not_2_out);
  and and_3 (Line_1_2, not_1_out, LSB);
  and and_4 (Line_0_2, not_1_out, not_2_out);
endmodule
