// Logisim project ex3d11p154.circ as structural Verilog: 1 circuit, main circuit main
module main (
  input  X,
  input  Y,
  input  Z,
  output out_4,
  output out_5
);

  wire not_1_out, not_2_out, not_3_out, x_prime_y_prime_z_out, x_prime_y_z_out, x_y_prime_z_out,
       x_y_prime_z_prime_out, x_y_z_out, xy_prime_z_prime_out;

  not not_1 (not_1_out, X);
  not not_2 (not_2_out, Y);
  not not_3 (not_3_out, Z);
  and x_prime_y_prime_z (x_prime_y_prime_z_out, not_1_out, not_2_out, Z);
  and x_prime_y_z (x_prime_y_z_out, not_1_out, Y, Z);
  and x_y_prime_z_prime (x_y_prime_z_prime_out, X, not_2_out, not_3_out);
  and x_y_prime_z (x_y_prime_z_out, X, not_2_out, Z);
  and x_y_z (x_y_z_out, X, Y, Z);
  and xy_prime_z_prime (xy_prime_z_prime_out, X, not_2_out, not_3_out);
  or or_1 (out_4, x_prime_y_prime_z_out, x_prime_y_z_out, x_y_prime_z_prime_out, x_y_prime_z_out, x_y_z_out);
  or or_2 (out_5, Z, xy_prime_z_prime_out);
endmodule
