// Logisim project table3d4p140.circ as structural Verilog: 1 circuit, main circuit main
module main (
  input  X,
  input  Y,
  input  Z,
  output out_4,
  output out_5
);

  wire and_1_out, and_2_out, and_3_out, and_4_out, and_5_out, and_6_out, not_1_out, not_2_out, not_3_out;

  not not_1 (not_1_out, X);
  not not_2 (not_2_out, Y);
  not not_3 (not_3_out, Z);
  and and_1 (and_1_out, not_2_out, Z);
  and and_2 (and_2_out, not_1_out, not_2_out, Z);
  and and_3 (and_3_out, X, not_2_out, not_3_out);
  and and_4 (and_4_out, X, not_2_out, Z, Z);
  and and_5 (and_5_out, X, Y, not_3_out);
  and and_6 (and_6_out, X, Y, Z);
  or or_1 (out_4, X, and_1_out);
  or or_2 (out_5, and_2_out, and_3_out, and_4_out, and_5_out, and_6_out);
endmodule
